# Fritzing sketch SMS_GAS_LEAK_ACCIDENT_PREVENTION_SYSTEM (saved by Fritzing 0.9.4)
breadboards: 3

parts:
  A1 = A9G GSM/GPRS+GPS Module
  M1 = DOIT Esp32 DevKit v1 (30 pins long, 11 pins width) [part_number=ESP32S-PIN30]
  U1 = GAS_SENSOR [package=mq-3]
  J1 = Basic Servo
  LED1 = smd LED [color="Red (633nm)" package="1206 [SMD]"]
  LED2 = RGB LED (com. anode, rbg) [package="5 mm [THT]"]
  J2 = Piezo Speaker

nets:
  N1: A1.Pin_1, A1.Pin_42
  N2: A1.Pin_2, A1.Pin_41
  N3: A1.Pin_3, A1.Pin_4, A1.Pin_5, A1.Pin_24, A1.Pin_25, A1.Pin_26, A1.Pin_27, A1.Pin_28, M1.GND, U1.H1, LED1.cathode, LED2.green_cathode, J2.pin1
  N4: A1.Pin_6, M1.VIN, U1.H2
  N5: A1.Pin_18, A1.Pin_19, A1.Pin_20, A1.Pin_21
  N6: M1.D34, J1.pulse
  N7: M1.D25, U1.A1
  N8: M1.D26, LED1.anode
  N9: M1.D27, LED2.common_anode
  N10: M1.D14, J2.pin2

custom parts:
  A9G GSM/GPRS+GPS Module: A9G is a complete quad-band GSM/GPRS+GPS module based on the RDA8955 chip.
  DOIT Esp32 DevKit v1 (30 pins long, 11 pins width): The DOIT Esp32 DevKit v1 is one of the development board created by DOIT to evaluate the ESP-WROOM-32 module. It is based on the ESP32 microcontroller that boasts Wifi, Bluetooth, Ethernet and Low Power support all in a single chip. (vanepp) made breadboard work, adjusted pin numbering and labels and reduced size of schematic and cleaned up pcb. This chip is 30pins long (2 x15) and 11 pins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
